# Fritzing sketch SketchState1 (saved by Fritzing 0.9.4)
breadboards: 1

parts:
  VCC1 = 4 x AAA Battery Mount  # not connected
  M1 = DC Motor
  M2 = DC Motor

nets:
  N1: M1.pin_1, M2.pin_1
  N2: M1.pin_2, M2.pin_2
